# Fritzing sketch SC mining controller schematic (fritzing) (saved by Fritzing 0.9.6b)

parts:
  Micro_Pro_Arduino1 = Micro Pro Arduino
  Slider_2_(active) = Slide Potentiometer [maximum_resistance=100kΩ]
  Slider_1_(reserve) = Slide Potentiometer [maximum_resistance=100kΩ]
  Toggle_1_(two-way) = Taiway 100-SP-X-T1 SPDT Miniature Toggle Switch [part_number=100-SP-X-T1-0-0-B1-M2 package=THT]
  Toggle_2_(one-way_capped) = Taiway 100-SP-X-T1 SPDT Miniature Toggle Switch [part_number=100-SP-X-T1-0-0-B1-M2 package=THT]
  Button_1_(green) = Round Pushbutton
  Button_2_(yellow) = Round Pushbutton
  Button_3_(red) = Round Pushbutton
  Button_4_(blue) = Round Pushbutton
  Button_5_(green) = Round Pushbutton
  Button_6_(red) = Square Pushbutton
  Button_7_(red) = Square Pushbutton
  Button_8_(red) = Square Pushbutton

nets:
  N1: Micro_Pro_Arduino1.pin_5, Button_1_(green).leg1
  N2: Micro_Pro_Arduino1.pin_6, Button_2_(yellow).leg1
  N3: Micro_Pro_Arduino1.pin_7, Button_5_(green).leg1
  N4: Micro_Pro_Arduino1.pin_8, Button_4_(blue).leg1
  N5: Micro_Pro_Arduino1.pin_9, Button_3_(red).leg1
  N6: Micro_Pro_Arduino1.pin_10, Button_8_(red).leg1
  N7: Micro_Pro_Arduino1.pin_11, Button_7_(red).leg1
  N8: Micro_Pro_Arduino1.pin_12, Button_6_(red).leg1
  N9: Micro_Pro_Arduino1.pin_14, Toggle_2_(one-way_capped).L2
  N10: Micro_Pro_Arduino1.pin_15, Toggle_1_(two-way).L2
  N11: Micro_Pro_Arduino1.pin_16, Toggle_1_(two-way).L1
  N12: Micro_Pro_Arduino1.pin_17, Slider_2_(active).wiper
  N13: Micro_Pro_Arduino1.pin_18, Slider_1_(reserve).wiper
  N14: Micro_Pro_Arduino1.pin_23, Slider_2_(active).leg1, Slider_1_(reserve).leg1, Toggle_1_(two-way).COM, Toggle_2_(one-way_capped).COM, Button_1_(green).leg0, Button_2_(yellow).leg0, Button_3_(red).leg0, Button_4_(blue).leg0, Button_5_(green).leg0, Button_6_(red).leg0, Button_7_(red).leg0, Button_8_(red).leg0
  N15: Micro_Pro_Arduino1.pin_24, Slider_2_(active).leg2, Slider_1_(reserve).leg2

custom parts:
  Micro Pro Arduino: A 32u4 based Arduino board
